# Fritzing sketch sketch (saved by Fritzing 1.0.4)
breadboards: 1

parts:
  M1 = Arduino NANO RP2040 CONNECT with headers
  M2 = DC Motor [voltage_(max)=5V voltage_(min)=3V]  # not connected
  A1 = Esp32-c3 super mini
  S2 = Pushbutton [package="[THT]"]
  S3 = Pushbutton [package="[THT]"]
  S4 = Pushbutton [package="[THT]"]
  S5 = Pushbutton [package="[THT]"]
  S6 = Pushbutton [package="[THT]"]
  S7 = Pushbutton [package="[THT]"]
  S8 = Pushbutton [package="[THT]"]
  S1 = Pushbutton [package="[THT]"]
  Power_plug1 = Power plug
  Q1 = Basic FET P-Channel [package="TO220 [THT]"]  # not connected
  M3 = DC Motor [voltage_(max)=5V voltage_(min)=3V]  # not connected
  M4 = DC Motor [voltage_(max)=5V voltage_(min)=3V]  # not connected
  M5 = DC Motor [voltage_(max)=5V voltage_(min)=3V]  # not connected
  Q2 = Basic FET P-Channel [package="TO220 [THT]"]  # not connected
  Q3 = Basic FET P-Channel [package="TO220 [THT]"]  # not connected
  Q4 = Basic FET P-Channel [package="TO220 [THT]"]  # not connected
  Bauteil2 = VL530X Time of Flight Distance Sensor [part_number="tonetoys #3317"]
  Bauteil3 = VL530X Time of Flight Distance Sensor [part_number="tonetoys #3317"]

nets:
  GND: M1.GND-4, M1.GND-29, A1.Pin_15, Power_plug1.GND, Bauteil2.GND, Bauteil3.GND
  VCC: M1.+5V, A1.Pin_16, Power_plug1.VCC, Bauteil2.VCC, Bauteil3.VCC
  N1: A1.Pin_6, S6.Pin_3
  N2: A1.Pin_7, S7.Pin_3, S7.Pin_4
  N3: A1.Pin_8, S8.Pin_3, S8.Pin_4
  N4: A1.Pin_9, S5.Pin_3, S5.Pin_4
  N5: A1.Pin_10, S4.Pin_3, S4.Pin_4
  N6: A1.Pin_11, S3.Pin_3
  N7: A1.Pin_12, S2.Pin_3
  N8: A1.Pin_13, S1.Pin_3
  N9: S2.Pin_1, S2.Pin_2, S3.Pin_1, S3.Pin_2, S4.Pin_1, S4.Pin_2, S5.Pin_1, S5.Pin_2, S6.Pin_1, S6.Pin_2, S7.Pin_1, S7.Pin_2, S8.Pin_1, S8.Pin_2, S1.Pin_1

notes:
  5V

custom parts:
  Esp32-c3 super mini: ESP32-C3 Development Board ESP32 SuperMini Development Board ESP32 Development Board WiFi Bluetooth.
  VL530X Time of Flight Distance Sensor: TOF
